// Logisim project Project 18 Parallel Sort.circ as structural Verilog: 2 circuits, main circuit main
module main (
  input  [3:0] In0,
  input  [3:0] In1,
  input  [3:0] In2,
  input  [3:0] In3,
  output [3:0] Out0,
  output [3:0] Out1,
  output [3:0] Out2,
  output [3:0] Out3
);

  wire Clear_button_out, Clock_out;
  wire [3:0] exchanger4_1_bigger, exchanger4_1_smaller, exchanger4_2_bigger, exchanger4_2_smaller,
       exchanger4_3_bigger, exchanger4_3_smaller, exchanger4_4_bigger, exchanger4_4_smaller,
       exchanger4_5_bigger, exchanger4_5_smaller;

  Exchanger4 exchanger4_1 (.Input_A(In0), .Input_B(In1), .Bigger(exchanger4_1_bigger), .Smaller(exchanger4_1_smaller));
  Exchanger4 exchanger4_2 (.Input_A(In2), .Input_B(In3), .Bigger(exchanger4_2_bigger), .Smaller(exchanger4_2_smaller));
  Exchanger4 exchanger4_3 (
    .Input_A(exchanger4_1_bigger), .Input_B(exchanger4_2_bigger), .Bigger(exchanger4_3_bigger),
    .Smaller(exchanger4_3_smaller));
  Exchanger4 exchanger4_4 (
    .Input_A(exchanger4_1_smaller), .Input_B(exchanger4_2_smaller), .Bigger(exchanger4_4_bigger),
    .Smaller(exchanger4_4_smaller));
  Exchanger4 exchanger4_5 (
    .Input_A(exchanger4_3_smaller), .Input_B(exchanger4_4_bigger), .Bigger(exchanger4_5_bigger),
    .Smaller(exchanger4_5_smaller));
  Clock Clock (.out(Clock_out));
  Register #(.width(4)) register_1 (
    .D(exchanger4_3_bigger), .Q(Out0), .clk(Clock_out), .clr(Clear_button_out));  // open: en
  Register #(.width(4)) register_2 (
    .D(exchanger4_5_bigger), .Q(Out1), .clk(Clock_out), .clr(Clear_button_out));  // open: en
  Register #(.width(4)) register_3 (
    .D(exchanger4_5_smaller), .Q(Out2), .clk(Clock_out), .clr(Clear_button_out));  // open: en
  Register #(.width(4)) register_4 (
    .D(exchanger4_4_smaller), .Q(Out3), .clk(Clock_out), .clr(Clear_button_out));  // open: en
  Button Clear_button (.out(Clear_button_out));
endmodule

module Exchanger4 (
  input  [3:0] Input_A,
  input  [3:0] Input_B,
  output [3:0] Bigger,
  output [3:0] Smaller
);

  wire comparator_1_gt, comparator_1_lt, not_1_out, not_2_out;

  Comparator #(.width(4), .mode("unsigned")) comparator_1 (
    .a(Input_A), .b(Input_B), .gt(comparator_1_gt), .lt(comparator_1_lt));  // open: eq
  assign Bigger = comparator_1_gt ? Input_A : 4'bz;  // Controlled_Buffer controlled_buffer_1
  assign Bigger = not_1_out ? Input_B : 4'bz;  // Controlled_Buffer controlled_buffer_2
  not not_1 (not_1_out, comparator_1_gt);
  assign Smaller = comparator_1_lt ? Input_A : 4'bz;  // Controlled_Buffer controlled_buffer_3
  assign Smaller = not_2_out ? Input_B : 4'bz;  // Controlled_Buffer controlled_buffer_4
  not not_2 (not_2_out, comparator_1_lt);
endmodule
